# Fritzing sketch Magnetic-Stirrer-Fritzing (saved by Fritzing 0.9.9b)
breadboards: 1

parts:
  Power_plug_-_12V = Power plug
  M1_Fan = DC Motor
  R1_-_100_ohm_potmeter = Rotary Potentiometer (Small) [maximum_resistance=100Ω package=THT]

nets:
  N1: Power_plug_-_12V.GND, M1_Fan.pin_2, R1_-_100_ohm_potmeter.leg1

notes:
  5V power supply
  Fan
  Potmeter（100Ω）
  This circuit works, but it does not account for voltage fluctuations at all, so it sometimes produces smoke.
  Please attach a switch in front of the fan or adjust the resistance yourself.
